# Fritzing sketch IR_LED_Driver_Circuit (saved by Fritzing 1.0.1rc)
breadboards: 1

parts:
  Q1 = NPN-Transistor [part_number=2N2222 package="TO92 [THT]"]
  R1 = Resistor [tolerance=±5% power=0.25 resistance=330 package=THT]
  D1 = LTE-302 [part_number="IR LED" package=lte-302]
  R2 = Resistor [tolerance=±5% power=0.25 resistance=10 package=THT]

nets:
  GND: Q1.E
  N1: Q1.B, R1.Pin_1
  N2: Q1.C, D1.C
  GPIO PIN: R1.Pin_0
  N3: D1.A, R2.Pin_1
  5V: R2.Pin_0
